// Logisim project 1_ Bit Adder.circ as structural Verilog: 13 circuits, main circuit 1_Bit Adder
module _1_Bit_Adder (
  input  A,
  input  B,
  input  Cin,
  output Q,
  output Cout
);

  wire nand_1_out, nand_2_out, nand_3_out, nand_5_out, nand_6_out, nand_7_out, nand_8_out, not_1_out,
       not_2_out, not_3_out;

  not not_1 (not_1_out, A);
  not not_2 (not_2_out, B);
  not not_3 (not_3_out, Cin);
  nand nand_1 (nand_1_out, not_1_out, not_2_out, Cin);
  nand nand_2 (nand_2_out, not_1_out, B, not_3_out);
  nand nand_3 (nand_3_out, A, B, Cin);
  nand nand_4 (Q, nand_1_out, nand_2_out, nand_3_out, nand_5_out);
  nand nand_5 (nand_5_out, A, not_2_out, not_3_out);
  nand nand_6 (nand_6_out, A, B);
  nand nand_7 (nand_7_out, B, Cin);
  nand nand_8 (nand_8_out, A, Cin);
  nand nand_9 (Cout, nand_6_out, nand_8_out, nand_7_out);
endmodule

module _8_Bit_Adder (
  input  [7:0] A,
  input  [7:0] B,
  input  Cin,
  output Cout,
  output [7:0] out_5,
  output out_6
);

  wire n1_bit_adder_2_cout, n1_bit_adder_3_cout, n1_bit_adder_4_cout, n1_bit_adder_5_cout,
       n1_bit_adder_6_cout, n1_bit_adder_7_cout, n1_bit_adder_8_cout;

  xor xor_1 (out_6, Cout, n1_bit_adder_2_cout);
  _1_Bit_Adder u_1_bit_adder_1 (.A(A[7]), .B(B[7]), .Cin(n1_bit_adder_2_cout), .Q(out_5[7]), .Cout(Cout));
  _1_Bit_Adder u_1_bit_adder_2 (
    .A(A[6]), .B(B[6]), .Cin(n1_bit_adder_3_cout), .Q(out_5[6]), .Cout(n1_bit_adder_2_cout));
  _1_Bit_Adder u_1_bit_adder_3 (
    .A(A[5]), .B(B[5]), .Cin(n1_bit_adder_4_cout), .Q(out_5[5]), .Cout(n1_bit_adder_3_cout));
  _1_Bit_Adder u_1_bit_adder_4 (
    .A(A[4]), .B(B[4]), .Cin(n1_bit_adder_5_cout), .Q(out_5[4]), .Cout(n1_bit_adder_4_cout));
  _1_Bit_Adder u_1_bit_adder_5 (
    .A(A[3]), .B(B[3]), .Cin(n1_bit_adder_6_cout), .Q(out_5[3]), .Cout(n1_bit_adder_5_cout));
  _1_Bit_Adder u_1_bit_adder_6 (
    .A(A[2]), .B(B[2]), .Cin(n1_bit_adder_7_cout), .Q(out_5[2]), .Cout(n1_bit_adder_6_cout));
  _1_Bit_Adder u_1_bit_adder_7 (
    .A(A[1]), .B(B[1]), .Cin(n1_bit_adder_8_cout), .Q(out_5[1]), .Cout(n1_bit_adder_7_cout));
  _1_Bit_Adder u_1_bit_adder_8 (.A(A[0]), .B(B[0]), .Cin(Cin), .Q(out_5[0]), .Cout(n1_bit_adder_8_cout));
endmodule

module Arithmetic_Unit (
  input  [7:0] B,
  input  Cin,
  input  [7:0] A,
  input  [2:0] SEL_OP,
  output Cout,
  output V,
  output [7:0] Q
);

  wire multiplexer_3_out, not_3_out;
  wire [7:0] multiplexer_1_out, multiplexer_2_out, not_1_out, not_2_out;

  assign not_1_out = ~A;  // NOT_Gate not_1, 8 bits wide
  Multiplexer #(.select(3), .width(8)) multiplexer_1 (
    .in0(A), .in1(A), .in2(A), .in3(A), .in4(not_1_out), .in5(A), .in6(A), .in7({8{1'b0}}),
    .out(multiplexer_1_out), .sel(SEL_OP));  // open: en
  assign not_2_out = ~B;  // NOT_Gate not_2, 8 bits wide
  Multiplexer #(.select(3), .width(8)) multiplexer_2 (
    .in0(B), .in1(B), .in2(8'h1), .in3({8{1'b1}}), .in4(8'h1), .in5(not_2_out), .in6(not_2_out), .in7(B),
    .out(multiplexer_2_out), .sel(SEL_OP));  // open: en
  _8_Bit_Adder u_8_bit_adder_1 (
    .A(multiplexer_1_out), .B(multiplexer_2_out), .Cout(Cout), .out_6(V), .Cin(multiplexer_3_out), .out_5(Q));
  Multiplexer #(.select(3)) multiplexer_3 (
    .in0(1'b0), .in1(Cin), .in2(1'b0), .in3(1'b0), .in4(1'b0), .in5(1'b1), .in6(not_3_out), .in7(1'b0),
    .out(multiplexer_3_out), .sel(SEL_OP));  // open: en
  not not_3 (not_3_out, Cin);

  // Notes on the sheet:
  //   000=ADD
  //   001=ADC
  //   010=INC
  //   011=DEC
  //   100=NEG
  //   101=SUB
  //   110=SBC
  //   111=MOV
endmodule

module Logic_Unit (
  input  Cin,
  input  [7:0] A,
  input  [7:0] B,
  input  [2:0] SEL_OP,
  output Cout,
  output [7:0] Q
);

  wire lsl_1_cout, lsr_1_cout, rol_1_cout, ror_1_cout;
  wire [7:0] AND_out, lsl_1_q, lsr_1_q, NOT_out, OR_out, rol_1_q, ror_1_q, XOR_out;

  assign OR_out = A | B;  // OR_Gate OR, 8 bits wide
  assign AND_out = A & B;  // AND_Gate AND, 8 bits wide
  Multiplexer #(.select(3), .width(8), .enable("false")) multiplexer_1 (
    .in0(AND_out), .in1(OR_out), .in2(XOR_out), .in3(NOT_out), .in4(lsl_1_q), .in5(lsr_1_q), .in6(rol_1_q),
    .in7(ror_1_q), .out(Q), .sel(SEL_OP));
  assign NOT_out = ~A;  // NOT_Gate NOT, 8 bits wide
  assign XOR_out = A ^ B;  // XOR_Gate XOR, 8 bits wide
  LSL lsl_1 (.Cout(lsl_1_cout), .A(A), .Q(lsl_1_q));
  ROL rol_1 (.Cout(rol_1_cout), .A(A), .Cin(Cin), .Q(rol_1_q));
  LSR lsr_1 (.Cout(lsr_1_cout), .A(A), .Q(lsr_1_q));
  ROR ror_1 (.Cin(Cin), .Cout(ror_1_cout), .A(A), .Q(ror_1_q));
  Multiplexer #(.select(3), .enable("false")) multiplexer_2 (
    .in0(Cin), .in1(Cin), .in2(Cin), .in3(Cin), .in4(lsl_1_cout), .in5(lsr_1_cout), .in6(rol_1_cout),
    .in7(ror_1_cout), .out(Cout), .sel(SEL_OP));
endmodule

module LSL (
  input  [7:0] A,
  output Cout,
  output [7:0] Q
);


  assign Cout = A[7];
  assign Q = {A[6:0], 1'b0};
endmodule

module LSR (
  input  [7:0] A,
  output Cout,
  output [7:0] Q
);


  assign Cout = A[0];
  assign Q = {1'b0, A[7:1]};
endmodule

module ROL (
  input  [7:0] A,
  input  Cin,
  output Cout,
  output [7:0] Q
);


  assign Cout = A[7];
  assign Q = {A[6:0], Cin};
endmodule

module ROR (
  input  [7:0] A,
  input  Cin,
  output Cout,
  output [7:0] Q
);


  assign Cout = A[0];
  assign Q = {Cin, A[7:1]};
endmodule

module ALU (
  input  [7:0] A,
  input  [7:0] B,
  input  [3:0] SREG_IN_VNZC,
  input  [3:0] SEL_OP,
  output [3:0] SREG_OUT_VNZC,
  output [7:0] Q
);

  wire arithmetic_unit_1_cout, arithmetic_unit_1_v, logic_unit_1_cout;
  wire [7:0] arithmetic_unit_1_q, logic_unit_1_q;

  Arithmetic_Unit arithmetic_unit_1 (
    .SEL_OP(SEL_OP[2:0]), .Cout(arithmetic_unit_1_cout), .V(arithmetic_unit_1_v), .A(A), .B(B),
    .Cin(SREG_IN_VNZC[0]), .Q(arithmetic_unit_1_q));
  Multiplexer #(.width(8), .enable("false")) multiplexer_1 (
    .in0(arithmetic_unit_1_q), .in1(logic_unit_1_q), .out(Q), .sel(SEL_OP[3]));
  Logic_Unit logic_unit_1 (
    .SEL_OP(SEL_OP[2:0]), .Cout(logic_unit_1_cout), .A(A), .B(B), .Cin(SREG_IN_VNZC[0]), .Q(logic_unit_1_q));
  nor nor_1 (SREG_OUT_VNZC[1], Q[7], Q[6], Q[5], Q[4], Q[3], Q[2], Q[1], Q[0]);
  Multiplexer #(.enable("false")) multiplexer_2 (
    .in0(arithmetic_unit_1_cout), .in1(logic_unit_1_cout), .out(SREG_OUT_VNZC[0]), .sel(SEL_OP[3]));
  Multiplexer #(.enable("false")) multiplexer_3 (
    .in0(arithmetic_unit_1_v), .in1(SREG_IN_VNZC[3]), .out(SREG_OUT_VNZC[3]), .sel(SEL_OP[3]));

  assign SREG_OUT_VNZC[2] = Q[7];

  // Notes on the sheet:
  //   0000=ADD
  //   0001=ADC
  //   0010=INC
  //   0011=DEC
  //   0100=NEG
  //   0101=SUB
  //   0110=SBC
  //   0111=MOV
  //   1000=AND
  //   1001=OR
  //   1010=XOR
  //   1011=NOT
  //   1100=LSL
  //   1101=LSR
  //   1110=ROL
  //   1111=ROR
endmodule

module GPR (
  input  [7:0] dataW,
  input  [2:0] addW,
  input  reset,
  input  CLK_W,
  input  WEnGPR,
  input  [2:0] addA,
  input  [2:0] addB,
  output [7:0] A,
  output [7:0] B
);

  wire and_1_out, decoder_1_out0, decoder_1_out1, decoder_1_out2, decoder_1_out3, decoder_1_out4,
       decoder_1_out5, decoder_1_out6, decoder_1_out7;
  wire [7:0] R0_q, R1_q, R2_q, R3_q, R4_q, R5_q, R6_q, R7_q;

  Decoder #(.select(3), .enable("false")) decoder_1 (
    .out0(decoder_1_out0), .out1(decoder_1_out1), .out2(decoder_1_out2), .out3(decoder_1_out3),
    .out4(decoder_1_out4), .out5(decoder_1_out5), .out6(decoder_1_out6), .out7(decoder_1_out7), .sel(addW));
  and and_1 (and_1_out, CLK_W, WEnGPR);
  Register R0 (.D(dataW), .en(decoder_1_out0), .Q(R0_q), .clk(and_1_out), .clr(reset));
  Register R4 (.D(dataW), .en(decoder_1_out4), .Q(R4_q), .clk(and_1_out), .clr(reset));
  Multiplexer #(.select(3), .width(8), .enable("false")) multiplexer_1 (
    .in0(R0_q), .in1(R1_q), .in2(R2_q), .in3(R3_q), .in4(R4_q), .in5(R5_q), .in6(R6_q), .in7(R7_q), .out(A),
    .sel(addA));
  Register R1 (.D(dataW), .en(decoder_1_out1), .Q(R1_q), .clk(and_1_out), .clr(reset));
  Register R5 (.D(dataW), .en(decoder_1_out5), .Q(R5_q), .clk(and_1_out), .clr(reset));
  Register R2 (.D(dataW), .en(decoder_1_out2), .Q(R2_q), .clk(and_1_out), .clr(reset));
  Register R6 (.D(dataW), .en(decoder_1_out6), .Q(R6_q), .clk(and_1_out), .clr(reset));
  Multiplexer #(.select(3), .width(8), .enable("false")) multiplexer_2 (
    .in0(R0_q), .in1(R1_q), .in2(R2_q), .in3(R3_q), .in4(R4_q), .in5(R5_q), .in6(R6_q), .in7(R7_q), .out(B),
    .sel(addB));
  Register R3 (.D(dataW), .en(decoder_1_out3), .Q(R3_q), .clk(and_1_out), .clr(reset));
  Register R7 (.D(dataW), .en(decoder_1_out7), .Q(R7_q), .clk(and_1_out), .clr(reset));
endmodule

module CPU (
  input  [7:0] ValueFromRAM,
  input  [15:0] FLASH_DATA,
  input  CLOCK,
  input  RESET,
  output [3:0] adressRAM,
  output [7:0] dataToRAM,
  output wEn_RAM,
  output rEn_RAM,
  output [7:0] FLASH_ADRESS
);

  wire id_1_en_jmp_br, id_1_flag_cmp, id_1_force_jmp, id_1_sreg_wen, id_1_wen_gpr, multiplexer_2_out,
       multiplexer_4_out, not_1_out, or_1_out, xnor_1_out;
  wire [1:0] id_1_flag_sel, id_1_gpr_ss;
  wire [2:0] id_1_out_8, id_1_reg_b;
  wire [3:0] alu_1_sreg_out_vnzc, id_1_alu_op_sel, SREG_q;
  wire [7:0] adder_1_out, alu_1_q, gpr_1_b, id_1_bot_8, multiplexer_1_out, multiplexer_3_out;
  wire [15:0] IR_q;

  ID id_1 (
    .Instruction(IR_q), .ADRESS_RAM(adressRAM), .ALU_OP_SEL(id_1_alu_op_sel), .BOT_8(id_1_bot_8),
    .flag_sel(id_1_flag_sel), .flag_cmp(id_1_flag_cmp), .out_8(id_1_out_8), .force_JMP(id_1_force_jmp),
    .rEn_RAM(rEn_RAM), .wEn_RAM(wEn_RAM), .en_JMP_BR(id_1_en_jmp_br), .sReg_wEn(id_1_sreg_wen),
    .wEn_GPR(id_1_wen_gpr), .GPR_SS(id_1_gpr_ss), .REG_B(id_1_reg_b));
  Register #(.width(16)) IR (.D(FLASH_DATA), .en(1'b1), .Q(IR_q), .clk(CLOCK));  // open: clr
  not not_1 (not_1_out, CLOCK);
  Adder adder_1 (.a(FLASH_ADRESS), .b(8'h1), .out(adder_1_out), .cin(1'b0));  // open: cout
  Multiplexer #(.width(8), .enable("false")) multiplexer_1 (
    .in0(adder_1_out), .in1(id_1_bot_8), .out(multiplexer_1_out), .sel(multiplexer_2_out));
  Register PC (.D(multiplexer_1_out), .en(1'b1), .Q(FLASH_ADRESS), .clk(not_1_out), .clr(RESET));
  Multiplexer #(.enable("false")) multiplexer_2 (
    .in0(1'b0), .in1(or_1_out), .out(multiplexer_2_out), .sel(id_1_en_jmp_br));
  GPR gpr_1 (
    .addW(id_1_out_8), .reset(RESET), .CLK_W(not_1_out), .WEnGPR(id_1_wen_gpr), .addA(id_1_out_8),
    .addB(id_1_reg_b), .dataW(multiplexer_3_out), .A(dataToRAM), .B(gpr_1_b));
  ALU alu_1 (
    .SEL_OP(id_1_alu_op_sel), .SREG_IN_VNZC(SREG_q), .SREG_OUT_VNZC(alu_1_sreg_out_vnzc), .A(dataToRAM),
    .B(gpr_1_b), .Q(alu_1_q));
  or or_1 (or_1_out, id_1_force_jmp, xnor_1_out);
  xnor xnor_1 (xnor_1_out, id_1_flag_cmp, multiplexer_4_out);
  Multiplexer #(.select(2), .width(8), .enable("false")) multiplexer_3 (
    .in0(id_1_bot_8), .in1(ValueFromRAM), .in2(alu_1_q), .in3({4'b0000, SREG_q}), .out(multiplexer_3_out),
    .sel(id_1_gpr_ss));
  Register #(.width(4)) SREG (.D(alu_1_sreg_out_vnzc), .en(id_1_sreg_wen), .Q(SREG_q), .clk(not_1_out), .clr(RESET));
  Multiplexer #(.select(2), .enable("false")) multiplexer_4 (
    .in0(SREG_q[0]), .in1(SREG_q[1]), .in2(SREG_q[2]), .in3(SREG_q[3]), .out(multiplexer_4_out),
    .sel(id_1_flag_sel));

  // Notes on the sheet:
  //   CZNV
endmodule

module ID (
  input  [15:0] Instruction,
  output [2:0] REG_B,
  output [3:0] ADRESS_RAM,
  output [3:0] ALU_OP_SEL,
  output [7:0] BOT_8,
  output [1:0] flag_sel,
  output flag_cmp,
  output [2:0] out_8,
  output force_JMP,
  output rEn_RAM,
  output wEn_RAM,
  output en_JMP_BR,
  output sReg_wEn,
  output wEn_GPR,
  output [1:0] GPR_SS
);

  ROM #(.addrWidth(4)) rom_1 (
    .addr(Instruction[15:12]), .data({GPR_SS, wEn_GPR, sReg_wEn, en_JMP_BR, wEn_RAM, rEn_RAM, force_JMP}));  // open: sel

  assign ADRESS_RAM = Instruction[3:0];
  assign ALU_OP_SEL = Instruction[7:4];
  assign BOT_8 = Instruction[7:0];
  assign flag_cmp = Instruction[10];
  assign flag_sel = Instruction[9:8];
  assign out_8 = Instruction[10:8];
  assign REG_B = Instruction[2:0];

  // Notes on the sheet:
  //   contents of rom_1 (hex, n*v repeats v):
  //   b0 10 20 62 4 9 8
endmodule

module MPU (
  input  in_1
);

  wire clock_1_out, cpu_1_ren_ram, cpu_1_wen_ram, not_1_out, or_1_out, RESET_out;
  wire [3:0] cpu_1_adressram;
  wire [7:0] cpu_1_datatoram, cpu_1_flash_adress, ram_1_data;
  wire [15:0] rom_1_data;

  ROM #(.dataWidth(16)) rom_1 (.addr(cpu_1_flash_adress), .data(rom_1_data));  // open: sel
  CPU cpu_1 (
    .FLASH_DATA(rom_1_data), .FLASH_ADRESS(cpu_1_flash_adress), .CLOCK(clock_1_out), .RESET(RESET_out),
    .adressRAM(cpu_1_adressram), .ValueFromRAM(ram_1_data), .dataToRAM(cpu_1_datatoram),
    .wEn_RAM(cpu_1_wen_ram), .rEn_RAM(cpu_1_ren_ram));
  Clock clock_1 (.out(clock_1_out));
  Button RESET (.out(RESET_out));
  not not_1 (not_1_out, clock_1_out);
  or or_1 (or_1_out, cpu_1_wen_ram, cpu_1_ren_ram);
  RAM #(.addrWidth(4), .bus("separate")) ram_1 (
    .addr(cpu_1_adressram), .din(cpu_1_datatoram), .data(ram_1_data), .str(cpu_1_wen_ram), .sel(or_1_out),
    .clk(not_1_out), .ld(cpu_1_ren_ram), .clr(in_1));

  // Notes on the sheet:
  //   contents of rom_1 (hex, n*v repeats v):
  //   2005 2106 1 1051 6500 4003 3203 5007
endmodule
